# Fritzing sketch schematic (saved by Fritzing 1.0.5)
breadboards: 1

parts:
  Part1 = Arduino Uno (Rev3) - ICSP
  R5 = Resistor [tolerance=±5% resistance=10k power=0.25W package=THT]
  D13 = Photocell (LDR) [package=THT]
  R8 = Photocell (LDR) [package=THT]
  R9 = Resistor [tolerance=±5% resistance=10k power=0.25W package=THT]
  common-GND = DC Motor [voltage_(max)=6V voltage_(min)=3V]
  7_4_V_18650_x_2_Li_ion_battery_/_BMS = DC Motor [voltage_(max)=6V voltage_(min)=3V]
  D2 = Photocell (LDR) [package=THT]
  R11 = Resistor [tolerance=±5% resistance=10k power=0.25W package=THT]
  S1 = Momentary Switch [package=ksa_sealed_tac_switch]
  R12 = Resistor [tolerance=±5% resistance=330 power=0.25W package=THT]
  LED1 = smd LED [color="Red (633nm)" package="0603 [SMD]"]
  VCC1 = Battery [internal_resistance=0.1Ω]
  5v = L298N DC motor driver

nets:
  5V: Part1.A0, Part1.5V, R5.Pin_1, D13.pin_0, R8.pin_0, R8.pin_1, D2.pin_1, 5v.5V
  N1: Part1.A1, D2.pin_0, R11.Pin_0
  N2: Part1.A2, D13.pin_1, R9.Pin_0
  N3: Part1.ICSP_MOSI, Part1.D11_PWM/MOSI, 5v.ENA
  N4: Part1.GND, R5.Pin_0, R9.Pin_1, R11.Pin_1, S1.3, S1.4, R12.Pin_1
  N5: Part1.D8, 5v.IN3
  N6: Part1.D9_PWM, 5v.IN2
  N7: Part1.D10_PWM/SS, 5v.IN1
  N8: Part1.D13/SCK, LED1.anode
  N9: Part1.D2, S1.1, S1.2
  N10: Part1.D6_PWM, 5v.ENB
  N11: Part1.D7, 5v.IN4
  N12: common-GND.pin_1, 5v.OUT4
  N13: common-GND.pin_2, 5v.OUT3
  N14: 7_4_V_18650_x_2_Li_ion_battery_/_BMS.pin_1, 5v.OUT2
  N15: 7_4_V_18650_x_2_Li_ion_battery_/_BMS.pin_2, 5v.OUT1
  N16: R12.Pin_0, LED1.cathode
  N17: VCC1.-, 5v.GND
  N18: VCC1.+, 5v.12V

custom parts:
  L298N DC motor driver: 2x DC motor driver with 78M05 positive voltage regulator (7..35 V) L298N: max 46 V, 2 A Set 5 V Enable jumper to enable 5 V regultor (needed for the L298N) and +5 V output at screw terminal or supply external +5 V at screw terminal Set ENA and/or ENB to +5 V to enable motor permanently or supply ENA and/or ENB with PWM signal IN1 and IN2 set rotation directory for motor A (OUT1/OUT2) IN2 and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
